# Fritzing sketch NeoPixel (saved by Fritzing 0.9.1b)
breadboards: 1

parts:
  Part1 = Photon
  Part2 = 16 NeoPixel Ring [part_number=1463]

nets:
  GND: Part1.GND, Part2.GND
  VIN: Part1.VIN, Part2.VDD
  N1: Part1.D0, Part2.IN

notes:
  G -> GND
  V+ -> 3v3 or Vin
  In -> Any PWM Pin (e.g. D0)

custom parts:
  16 NeoPixel Ring: 16 ultra bright smart LED NeoPixels are arranged in a circle with 1.75" (44.5mm) outer diameter. The rings are 'chainable' - connect the output pin of one to the input pin of another. Use only one microcontroller pin to control as many as you can chain together! Each LED is addressable as the driver chip is inside the LED. Each one has ~18mA constant current drive so the color will be very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
