# Fritzing sketch DCorVibrationMotorV2 (saved by Fritzing 0.9.1b)
breadboards: 1

parts:
  Part1 = Photon
  L1 = Solenoid
  Q1 = TIP120 Hi-Current Darlington Transistor
  VCC1 = 4 x AAA Battery Mount
  R1 = Resistor [tolerance=±5% resistance=1k package="0805 [SMD]"]
  D1 = Zener Diode [part_number=1N4732A breakdown_voltage=3.6V package="300 mil [THT]"]

nets:
  N1: Part1.GND, Q1.EMITTER, VCC1.-, D1.anode
  N2: Part1.D0, R1.Pin_1
  N3: L1.pin1, Q1.COLLECTOR, D1.cathode
  N4: L1.pin2, VCC1.+
  N5: Q1.BASE, R1.Pin_0
