# Fritzing sketch fritzing-diagram (saved by Fritzing 0.9.3b)
breadboards: 1

parts:
  Part1 = Photon
  R1 = Resistor [tolerance=±5% resistance=220 package=THT]
  R2 = Slide Potentiometer [maximum_resistance=10kΩ]
  J1 = Basic Force Sensing Resistor (FSR) [package=THT]
  R3 = Resistor [tolerance=±5% resistance=220 package=THT]
  DFRobot_DFPlayer_Mini1 = DFRobot DFPlayer Mini [part_number=DFR0299]
  SP1 = SPEAKER [package=pcb_mount_speaker]
  LED1 = LED_RING [package=led_ring]
  J2 = Piezo Speaker

nets:
  N1: Part1.A2, R3.Pin_1
  N2: Part1.RX, DFRobot_DFPlayer_Mini1.TX
  N3: Part1.TX, DFRobot_DFPlayer_Mini1.RX
  N4: Part1.GND, R1.Pin_0, R2.leg1, DFRobot_DFPlayer_Mini1.GND-1, DFRobot_DFPlayer_Mini1.GND-2, SP1.+, LED1.8, J2.pin1
  VIN: Part1.VIN, R2.leg2, J1.pin_1, DFRobot_DFPlayer_Mini1.VCC
  N5: Part1.D0, LED1.9
  N6: Part1.D2, J2.pin2
  N7: Part1.3V3, LED1.7
  N8: R1.Pin_1, R2.wiper
  N9: J1.pin_0, R3.Pin_0
  N10: DFRobot_DFPlayer_Mini1.DAC_R, SP1.-
